# Fritzing sketch electrical-wiring (saved by Fritzing 0.9.3b)

parts:
  LCD_Display = Standard LCD 16x2 white on blue
  ENCODER1 = Rotary Encoder with Knob
  R1 = Rotary Potentiometer (Small) [maximum_resistance=10kΩ package=THT]
  M0_Express = Itsy Bitsy M0 Express
  Red_Arcade_Button = Square Pushbutton

nets:
  GND: LCD_Display.VSS, LCD_Display.R/W, LCD_Display.LED-, ENCODER1.no_name_yet#3, R1.leg2
  N1: LCD_Display.VDD, LCD_Display.LED+, R1.leg1, M0_Express.VHI
  N2: LCD_Display.V0, R1.wiper
  N3: LCD_Display.RS, M0_Express.D7
  N4: LCD_Display.E, M0_Express.D9
  N5: LCD_Display.DB4, M0_Express.D13
  N6: LCD_Display.DB5, M0_Express.D12
  N7: LCD_Display.DB6, M0_Express.D11
  N8: LCD_Display.DB7, M0_Express.D10
  N9: ENCODER1.no_name_yet#1, M0_Express.D1
  N10: ENCODER1.no_name_yet#2, M0_Express.D0
  N11: M0_Express.GND, Red_Arcade_Button.leg1
  N12: M0_Express.D2, Red_Arcade_Button.leg0

custom parts:
  Standard LCD 16x2 white on blue: Standard HD44780 LCDs are useful for creating standalone projects. * 16 characters wide, 2 rows * White text on blue background * Connection port is 0.1" pitch, single row for easy breadboarding and wiring
  Rotary Encoder with Knob: Rotary Encoder with 1/4" Shaft and Knob
  Itsy Bitsy M0 Express: What's smaller than a Feather but larger than a Trinket? It's an Adafruit ItsyBitsy M0 Express! Small, powerful, with a rockin' ATSAMD21 Cortex M0 processor running at 48 MHz - this microcontroller board is perfect when you want something very compact, but still with a bunch of pins. ItsyBitsy M0 Express is only 1.4" long by 0.7" wide, but has 6 power pins, 23 digital GPIO pins (12 of which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
